// Logisim project Project.circ as structural Verilog: 1 circuit, main circuit main
module main (
);

  wire _15_bit_Shift_Register_out, and_1_out, and_2_out, and_3_out, CLK_out, En_out, not_1_out;
  wire [3:0] T0_q;

  Clock CLK (.out(CLK_out));
  Shift_Register #(.length(15)) _15_bit_Shift_Register (
    .shift(1'b1), .in(not_1_out), .clk(CLK_out), .out(_15_bit_Shift_Register_out));  // open: load, clr, d0, q0, d1, q1, d2, q2, d3, q3, d4, q4, d5, q5, d6, q6, d7, q7, d8, q8, d9, q9, d10, q10, d11, q11, d12, q12, d13, q13, d14, q14
  not not_1 (not_1_out, 1'b1);
  and En (En_out, 1'b1, _15_bit_Shift_Register_out);
  and and_1 (and_1_out, T0_q[0], En_out);
  and and_2 (and_2_out, T0_q[1], and_1_out);
  and and_3 (and_3_out, T0_q[2], and_2_out);
  T_Flip_Flop T0 (.clk(CLK_out), .T(En_out), .Q(T0_q[0]));  // open: Qn, preset, reset, en
  T_Flip_Flop T1 (.clk(CLK_out), .T(and_1_out), .Q(T0_q[1]));  // open: Qn, preset, reset, en
  T_Flip_Flop T2 (.clk(CLK_out), .T(and_2_out), .Q(T0_q[2]));  // open: Qn, preset, reset, en
  T_Flip_Flop T3 (.clk(CLK_out), .T(and_3_out), .Q(T0_q[3]));  // open: Qn, preset, reset, en
  Hex_Digit_Display hex_digit_display_1 (.value(T0_q));  // open: dp
endmodule
